# Fritzing sketch pi-camera-breadboard-button (saved by Fritzing 0.9.9b)
breadboards: 1

parts:
  Part2 = Arduino Nano (Rev3.0) (ICSP)
  LED1 = LED - 3mm [color="Red (633nm)" current=0.030 package="3 mm [THT]"]
  R1 = Resistor [tolerance=±5% resistance=220 package="2512 [SMD]"]
  S1 = Momentary Switch [package=ksa_sealed_tac_switch]
  R2 = Resistor [tolerance=±5% resistance=10000 package="2512 [SMD]"]
  PIR_Sensor_HC-SR501 = HC-SR501 Body Sensor Module
  Raspberry_Pi_4 = Raspberry Pi 4B  # not connected
  Pi_Camera = TRANSCHIPTC5747 [package=camera_sfv24r-2st_2]  # not connected

nets:
  GND: Part2.GND, LED1.cathode, R2.Pin_1, PIR_Sensor_HC-SR501.GND
  N1: Part2.D2, S1.1
  N2: Part2.D5, R1.Pin_1
  N3: Part2.D8, PIR_Sensor_HC-SR501.OUT
  5V: Part2.5V, S1.4, PIR_Sensor_HC-SR501.VCC
  N4: LED1.anode, R1.Pin_0
  N5: S1.2, R2.Pin_0

custom parts:
  HC-SR501 Body Sensor Module: Pyroelectric Infrared PIR Motion Sensor Detector Module
